# Fritzing sketch Sketch_Sensor_luz_arduino (saved by Fritzing 0.8.7b)

parts:
  Componente2 = BlackBoard v1.1
  R1 = Photocell (LDR) [package=THT]
  Componente3 = SRF05 Ultrasonic Rangefinder
  Componente4 = Módulo Relé
  Componente5 = SRF05 Ultrasonic Rangefinder
  R2 = Resistor [tolerance=±5% resistance=10k package=THT]
  LED1 = LEDs [package=led10mm]

nets:
  N1: Componente2.A0, R1.pin_0, R2.Pin_0
  N2: Componente2.D8, Componente5.Echo
  N3: Componente2.D9_PWM, Componente5.Trig
  N4: Componente2.D10_PWM/SS, Componente3.Echo
  N5: Componente2.D11_PWM/MOSI, Componente3.Trig
  N6: Componente2.D7, Componente4.In
  5V: Componente2.5V, R1.pin_1, Componente3.VCC, Componente4.5V, Componente5.VCC
  GND: Componente2.GND, Componente3.GND, Componente4.GND, Componente5.GND, R2.Pin_1
  N7: Componente4.C, LED1.A

custom parts:
  BlackBoard v1.1: Esta é a BlackBoard, a placa Arduino compatível fabricada pela RoboCore. Ela foi projetada unindo o melhor das placas Arduino básicas lançadas até hoje, além de algumas melhorias feitas pelos nossos engenheiros. Veja abaixo as vantagens desta placa para a Arduino UNO R3: Suporta maior drenagem de corrente elétrica em seu pino de 5V (suporta um maior número de periféricos ligados a ela, sem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
  Módulo Relé: Este modulo pode ser usado em diversos projetos afim de acionar cargas de até 250VAC @ 7A ou 125VAC @ 10A. Pode ser usado para controlar luzes, equipamentos ligados a rede elétrica, motores, etc. Você pode fazer uma ponte-H baseada em relés com alguns destes módulos.
  LEDs: LEDs Standard schematic elements and footprints for 5mm, 3mm, 1206, and 0603 sized LEDs. 5mm - Spark Fun Electronics SKU : COM-00529 (and others)
